// Logisim project HINTIND.circ as structural Verilog: 1 circuit, main circuit main
module main (
  input  CTLCLKE_AL,
  input  CNTLCLK,
  input  A43_OUT_SDTAR,
  input  A38_IN100,
  input  RGBS05,
  input  RGBS04,
  input  RGBS03
);

  wire and_1_out, and_2_out, and_3_out, and_4_out, d_ff_1_qn, d_ff_2_q, d_ff_2_qn, d_ff_3_qn, d_ff_4_qn,
       nand_1_out, nand_2_out, nor_1_out, not_1_out, not_2_out, not_3_out, not_4_out;

  D_Flip_Flop d_ff_1 (.D(1'b0), .clk(1'b0), .Qn(d_ff_1_qn), .preset(A43_OUT_SDTAR), .reset(not_1_out));  // open: Q
  not not_1 (not_1_out, not_2_out);
  not not_2 (not_2_out, A38_IN100);
  not not_3 (not_3_out, A43_OUT_SDTAR);
  and and_1 (and_1_out, not_3_out, RGBS05);
  and and_2 (and_2_out, d_ff_1_qn, d_ff_2_qn);
  and and_3 (and_3_out, CNTLCLK, not_4_out);
  nor nor_1 (nor_1_out, and_1_out, and_2_out);
  not not_4 (not_4_out, CTLCLKE_AL);
  D_Flip_Flop d_ff_2 (.D(nor_1_out), .clk(and_3_out), .Q(d_ff_2_q), .Qn(d_ff_2_qn));  // open: preset, reset
  D_Flip_Flop d_ff_3 (.D(RGBS04), .clk(and_3_out), .Qn(d_ff_3_qn));  // open: Q, preset, reset
  D_Flip_Flop d_ff_4 (.D(RGBS03), .clk(and_3_out), .Qn(d_ff_4_qn));  // open: Q, preset, reset
  and and_4 (and_4_out, d_ff_2_q, d_ff_3_qn, d_ff_4_qn);
  nand nand_1 (nand_1_out, and_4_out, and_4_out);
  not nand_2 (nand_2_out, nand_1_out);  // NAND_Gate
  Pull_Resistor #(.pull(1)) pull_resistor_1 (.node(nand_1_out));
  LED HINTIND (.in(nand_1_out));

  // Notes on the sheet:
  //   nand_1 drives only 0 and floats otherwise
  //   APIF PG.3
endmodule
